# Fritzing sketch Autoclicker (saved by Fritzing 0.9.3b)
breadboards: 1

parts:
  Q1 = NPN-Transistor [package="TO92 [THT]"]
  Componente1 = Arduino Uno (Rev3) - ICSP

nets:
  N1: Q1.B, Componente1.D13/SCK
  N2: Q1.C, Componente1.GND

notes:
  Liaremos el final del cable con papel albal,
  y una moneda encima donde queremos que se reciban pulsos electricos.

// code stored in the sketch: Autoclicker.ino
void setup() {
  pinMode(13, OUTPUT);

}

void loop() {
  digitalWrite(13, HIGH);
  delay(30); //Frecuencia a la que se envian los pulsos. 
  digitalWrite(13, LOW);
  delay(30);
}
